# Fritzing sketch Watering (saved by Fritzing 0.9.4)
circuit board: 8.46667cm x 5.64444cm
breadboards: 1

parts:
  U1 = ESP8266 NodeMCU LoLin module
  sensor_3 = Soil Moisture Sensor
  sensor_2 = Soil Moisture Sensor
  sensor1 = Soil Moisture Sensor
  HT7333 = Voltage Regulator - 3.3V [package="TO220 [THT]"]
  2_Li-Ion_batteries = Battery block 9V
  C1 = Electrolytic Capacitor [capacitance=0.47mF package="100 mil [THT, electrolytic]"]
  C2 = Electrolytic Capacitor [capacitance=0.47mF package="100 mil [THT, electrolytic]"]
  Water_pump_1 = DC Motor
  M2 = DC Motor
  M3 = DC Motor
  Q1 = NPN-Transistor [package="TO92 [THT]"]
  R1 = Resistor [tolerance=±5% resistance=220 package=THT]
  R2 = Resistor [tolerance=±5% resistance=220 package=THT]
  R3 = Resistor [tolerance=±5% resistance=220 package=THT]
  Q2 = NPN-Transistor [package="TO92 [THT]"]
  Q3 = NPN-Transistor [package="TO92 [THT]"]

nets (from the schematic view):
  N1: U1.connector0, U1.connector17
  N2: U1.connector1, sensor1.VCC
  N3: U1.connector2, sensor_2.VCC
  N4: U1.connector3, sensor_3.VCC
  N5: U1.connector7, R3.Pin_0
  N6: U1.connector8, R2.Pin_0
  N7: U1.connector9, R1.Pin_0
  GND: U1.connector13, HT7333.GND, 2_Li-Ion_batteries.-, C1.-, C2.-, Q1.E, Q2.E, Q3.E
  N8: U1.connector19, HT7333.output_voltage, C2.+
  N9: U1.connector42, sensor_3.SIG, sensor_2.SIG, sensor1.SIG
  GND_2: sensor_3.GND, sensor_2.GND, sensor1.GND
  N10: HT7333.input_voltage, 2_Li-Ion_batteries.+, C1.+, Water_pump_1.pin_1, M2.pin_1, M3.pin_1
  N11: Water_pump_1.pin_2, Q1.C
  N12: M2.pin_2, Q2.C
  N13: M3.pin_2, Q3.C
  N14: Q1.B, R1.Pin_1
  N15: R2.Pin_1, Q2.B
  N16: R3.Pin_1, Q3.B
